# Fritzing sketch opstelling (saved by Fritzing 0.9.0b)
circuit board: 8.46667cm x 5.64444cm
breadboards: 1

parts:
  Onderdeel1 = Arduino Uno (Rev3)
  U1 = POT [package=pot_alpha_rv16af-20]
  Onderdeel2 = LED Matrix - Serial Interface - Red/Green/Blue

nets (from the schematic view):
  N1: Onderdeel1.A0, U1.S
  N2: Onderdeel1.A4/SDA, Onderdeel2.SCK
  N3: Onderdeel1.A5/SCL, Onderdeel2.MOSI
  GND: Onderdeel1.GND, U1.A, Onderdeel2.GND
  5V: Onderdeel1.5V, U1.E, Onderdeel2.VCC
